# Fritzing sketch schematics (saved by Fritzing 0.9.2b)
circuit board: 7.14762cm x 4.63193cm
breadboards: 1

parts:
  U1 = Voltage Regulator - 5V [package="TO220 [THT]"]
  U2 = atmega328 [package=dip]
  J1 = Power Jack [package=power_jack_smd]
  R2 = PHOTOCELL [package=photocell]
  PIR1 = PIR sensor
  Q1 = MOSFET-NCHANNEL [package=to220v]
  J2 = Power Jack [package=power_jack_smd]
  S1 = Momentary Switch [package=ksa_sealed_tac_switch]
  S3 = Momentary Switch [package=ksa_sealed_tac_switch]
  R1 = Resistor [tolerance=±5% resistance=220 package=THT]
  R3 = Resistor [tolerance=±5% resistance=1.5k package=THT]
  R4 = Resistor [tolerance=±5% resistance=1.5k package=THT]

nets:
  N1: U1.input_voltage, J1.PWR
  GND: U1.GND, U2.GND, J1.GND, PIR1.GND, Q1.S, R1.Pin_1, R3.Pin_0, R4.Pin_1
  VCC: U1.output_voltage, U2.VCC, U2.AVCC, R2.P$2, PIR1.VDD, J2.PWR, S1.4, S3.2
  N2: U2.D9_(PWM), Q1.G
  N3: U2.D10_(PWM), PIR1.SIG
  N4: U2.D11_(PWM), S3.4, R4.Pin_0
  N5: U2.D12, S1.2, R3.Pin_1
  N6: U2.A0, R2.P$1, R1.Pin_0
  N7: Q1.D, J2.GNDBREAK

notes:
  in the hall
  to led strip
  12V power
  add 10 minutes
  change brightness
